# Fritzing sketch 7Segment_Output (saved by Fritzing 0.9.2b)
breadboards: 1

parts:
  J1 = T Cobbler Plus
  7SEG1 = 7-Segment LED I2C Backpack (yellow)
  S1 = Pushbutton [package="[THT]"]  # not connected

nets:
  N1: J1.5.0V#1, 7SEG1.SDA
  N2: J1.SDA, 7SEG1.SCL
  N3: J1.MISO, 7SEG1.V+
  N4: J1.SCLK, 7SEG1.GND

custom parts:
  T Cobbler Plus: The T-Cobbler Plus is an add on prototyping board from Adafruit specifically designed for the Raspberry Pi B+ that can break out all those tasty power, GPIO, I2C and SPI pins from the 40-pin header onto a solderless breadboard. This set will make "cobbling together" prototypes with the Pi super easy. The T-Cobbler Plus can plug into any solderless breadboard.
  7-Segment LED I2C Backpack (yellow): 4-digit, 7-segment LED Display with I2C Control
