# Fritzing sketch Example 2 Input (saved by Fritzing 0.9.1b)
breadboards: 1

parts:
  Pi1 = Adafruit Pi Cobbler
  LED1 = LED - 5mm [color="Red (633nm)" package="5 mm [THT]"]
  R1 = Resistor [tolerance=±5% resistance=220 package=THT]
  S1 = Pushbutton [package="[THT]"]

nets:
  N1: Pi1.GND, R1.Pin_0
  N2: Pi1.#17, S1.Pin_3, S1.Pin_4
  N3: Pi1.#18, LED1.anode
  N4: Pi1.PIN19, S1.Pin_1, S1.Pin_2
  N5: LED1.cathode, R1.Pin_1

custom parts:
  Adafruit Pi Cobbler: Adafruit Pi Cobbler GPIO Breakout for Raspberry Pi
