# Fritzing sketch FullAdder (saved by Fritzing 0.9.1b)
breadboards: 1

parts:
  IC1 = IC, DIP package, 14 pins [chip_label=7408]
  IC2 = IC, DIP package, 14 pins [chip_label=7486]
  IC3 = IC, DIP package, 14 pins [chip_label=7432]
  J1 = T Cobbler Plus
  REG1 = LD33 Low-Dropout Voltage Regulator
  REG2 = LD33 Low-Dropout Voltage Regulator

nets:
  N1: IC1.pin1, IC2.pin5, J1.5.0V#3
  N2: IC1.pin2, IC2.pin3, IC2.pin4
  N3: IC1.pin3, IC3.pin1
  N4: IC1.pin4, IC2.pin1, J1.TXD
  N5: IC1.pin5, IC2.pin2, J1.GND#5
  N6: IC1.pin6, IC3.pin2
  GND: IC1.pin7, IC2.pin7, IC3.pin7, J1.SCL, REG1.GND, REG2.GND
  N7: IC1.pin14, IC2.pin14, IC3.pin14, J1.MISO
  N8: IC2.pin6, REG1.Vin
  N9: IC3.pin3, REG2.Vin
  N10: J1.EEC, REG1.Vout
  N11: J1.#5, REG2.Vout

custom parts:
  T Cobbler Plus: The T-Cobbler Plus is an add on prototyping board from Adafruit specifically designed for the Raspberry Pi B+ that can break out all those tasty power, GPIO, I2C and SPI pins from the 40-pin header onto a solderless breadboard. This set will make "cobbling together" prototypes with the Pi super easy. The T-Cobbler Plus can plug into any solderless breadboard.
