# Fritzing sketch GPIO LED Circuit (saved by Fritzing 0.9.1b)
breadboards: 1

parts:
  LED1 = LED - 5mm [color="Red (633nm)" package="5 mm [THT]"]
  R1 = Resistor [tolerance=±5% resistance=82 package=THT]
  J1 = T Cobbler Plus

nets:
  N1: LED1.cathode, R1.Pin_0
  N2: LED1.anode, J1.CE1
  N3: R1.Pin_1, J1.SCLK

custom parts:
  T Cobbler Plus: The T-Cobbler Plus is an add on prototyping board from Adafruit specifically designed for the Raspberry Pi B+ that can break out all those tasty power, GPIO, I2C and SPI pins from the 40-pin header onto a solderless breadboard. This set will make "cobbling together" prototypes with the Pi super easy. The T-Cobbler Plus can plug into any solderless breadboard.
