# Fritzing sketch binary (saved by Fritzing 0.9.3b)
breadboards: 1

parts:
  LED1 = LED - 5mm [color="Red (633nm)" package="5 mm [THT]"]
  J1 = T Cobbler Plus
  R1 = Resistor [tolerance=±5% resistance=82 package=THT]
  LED2 = LED - 5mm [color="Red (633nm)" package="5 mm [THT]"]
  LED3 = LED - 5mm [color="Red (633nm)" package="5 mm [THT]"]
  LED4 = LED - 5mm [color="Red (633nm)" package="5 mm [THT]"]
  R2 = Resistor [tolerance=±5% resistance=82 package=THT]
  R3 = Resistor [tolerance=±5% resistance=82 package=THT]

nets:
  N1: LED1.cathode, R1.Pin_0
  N2: LED1.anode, J1.TXD
  N3: J1.GND#5, LED3.anode, LED4.anode
  N4: J1.#4, LED2.anode
  N5: R1.Pin_1, R2.Pin_1, R3.Pin_1
  N6: LED2.cathode, R2.Pin_0
  N7: LED3.cathode, LED4.cathode, R3.Pin_0

custom parts:
  T Cobbler Plus: The T-Cobbler Plus is an add on prototyping board from Adafruit specifically designed for the Raspberry Pi B+ that can break out all those tasty power, GPIO, I2C and SPI pins from the 40-pin header onto a solderless breadboard. This set will make "cobbling together" prototypes with the Pi super easy. The T-Cobbler Plus can plug into any solderless breadboard.
