# Fritzing sketch led_button_circuit_rev3 (saved by Fritzing 0.9.3b)
breadboards: 1

parts:
  Part1 = Adafruit T-Cobbler Plus [part_number="Adafruit #1989 and #2028"]
  S2 = Pushbutton [package="[THT]"]
  LED2 = LED - 5mm [color="Red (633nm)" package="5 mm [THT]"]
  R2 = Resistor [tolerance=±5% resistance=82 package=THT]

nets:
  N1: Part1.+3.3V, S2.Pin_3, S2.Pin_4
  N2: Part1.GND, R2.Pin_0
  N3: Part1.GPIO17, S2.Pin_1, S2.Pin_2
  N4: Part1.GPIO18, LED2.anode
  N5: LED2.cathode, R2.Pin_1

custom parts:
  Adafruit T-Cobbler Plus: The Raspberry Pi has landed on the Maker World like a 40-GPIO pinned, quad-USB ported, credit card sized bomb of DIY joy. And while you can use most of our great Model B accessories by hooking up our downgrade cable, its probably a good time to upgrade your set up and accessorize using all of the 40 pins. That's why we now carry the Assembled Adafruit Pi T-Cobbler Plus - Breakout + Cable for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
