// Logisim project 7400_pinout.circ as structural Verilog: 1 circuit, main circuit main
module main (
  output _14,
  output _13,
  output _12,
  output _11,
  output _10,
  output _9,
  output _8,
  output _1,
  output _2,
  output _3,
  output _4,
  output _5,
  output _6,
  output _7
);

  // Probe on nothing
  nand nand_1 (_3, _1, _2);
  nand nand_2 (_11, _12, _13);
  nand nand_3 (_8, _9, _10);
  nand nand_4 (_6, _4, _5);

  assign _7 = 1'b0;
  assign _14 = 1'b1;

  // Notes on the sheet:
  //   vcc (+5v)
  //   gnd
endmodule
