# Fritzing sketch 7Segment_SpeedTest (saved by Fritzing 0.9.4)
breadboards: 1

parts:
  J1 = T Cobbler Plus
  Part1 = 0.56" 7-segment LED Backpack [part_number=880]

nets:
  3V3: J1.3V3, Part1.VDD
  N1: J1.5.0V#1, Part1.SDA
  N2: J1.SDA, Part1.SCL
  N3: J1.SCLK, Part1.GND

custom parts:
  T Cobbler Plus: The T-Cobbler Plus is an add on prototyping board from Adafruit specifically designed for the Raspberry Pi B+ that can break out all those tasty power, GPIO, I2C and SPI pins from the 40-pin header onto a solderless breadboard. This set will make "cobbling together" prototypes with the Pi super easy. The T-Cobbler Plus can plug into any solderless breadboard.
  0.56" 7-segment LED Backpack: This 0.56" 7-segment LED display includes a driver chip for simple control via an I2C interface. The backpack features address-selection jumpers so you can connect up to eight displays on a single I2C bus.
