// Logisim project half_adder.circ as structural Verilog: 1 circuit, main circuit main
module main (
  input  X,
  input  Y,
  output S,
  output C
);

  xor xor_1 (S, Y, X);
  and and_1 (C, Y, X);
endmodule
